# Fritzing sketch FritzingSketch (saved by Fritzing 0.9.3b)
breadboards: 4

parts:
  Part1 = Arduino Uno (Rev3)
  DFRobot_DFPlayer_Mini1 = DFRobot DFPlayer Mini [part_number=DFR0299]
  SP1 = SPEAKER [package=pcb_mount_speaker]
  R1 = Resistor [tolerance=±5% resistance=1k package=THT]
  U1 = 7-SEGMENT-DISPLAY [package=7-segment-display]
  U2 = 7-SEGMENT-DISPLAY [package=7-segment-display]
  U3 = 74HC595 [package="DIP16 [THT]"]
  U4 = 74HC595 [package="DIP16 [THT]"]
  S2 = Pushbutton [package="[THT]"]
  S5 = Pushbutton [package="[THT]"]
  LED3 = LED - 5mm [color="Blue (430nm)" package="5 mm [THT]"]
  LED4 = LED - 5mm [color="Green (555nm)" package="5 mm [THT]"]
  S6 = Pushbutton [package="[THT]"]
  S7 = Pushbutton [package="[THT]"]
  LED5 = LED - 5mm [color="Red (635nm)" package="5 mm [THT]"]
  LED6 = LED - 5mm [color="Blue (525nm)" package="5 mm [THT]"]
  S8 = Pushbutton [package="[THT]"]
  S9 = Pushbutton [package="[THT]"]
  LED7 = LED - 5mm [color="Green (570nm)" package="5 mm [THT]"]
  LED8 = LED - 5mm [color="Yellow (595nm)" package="5 mm [THT]"]
  S10 = Pushbutton [package="[THT]"]
  LED9 = LED - 5mm [color="Orange (620nm)" package="5 mm [THT]"]
  U5 = 74HC595 [package="DIP16 [THT]"]
  R2 = Resistor [tolerance=±5% resistance=220 package=THT]
  R3 = Resistor [tolerance=±5% resistance=220 package=THT]
  R4 = Resistor [tolerance=±5% resistance=220 package=THT]
  R5 = Resistor [tolerance=±5% resistance=220 package=THT]
  R6 = Resistor [tolerance=±5% resistance=220 package=THT]
  R7 = Resistor [tolerance=±5% resistance=220 package=THT]
  R8 = Resistor [tolerance=±5% resistance=220 package=THT]
  R9 = Resistor [tolerance=±5% resistance=220 package=THT]
  R10 = Resistor [tolerance=±5% resistance=220 package=THT]
  R11 = Resistor [tolerance=±5% resistance=220 package=THT]
  R13 = Resistor [tolerance=±5% resistance=220 package=THT]
  R14 = Resistor [tolerance=±5% resistance=220 package=THT]
  R15 = Resistor [tolerance=±5% resistance=220 package=THT]
  R16 = Resistor [tolerance=±5% resistance=220 package=THT]
  R17 = Resistor [tolerance=±5% resistance=220 package=THT]
  R18 = Resistor [tolerance=±5% resistance=220 package=THT]
  R19 = Resistor [tolerance=±5% resistance=220 package=THT]
  R20 = Resistor [tolerance=±5% resistance=220 package=THT]
  R21 = Resistor [tolerance=±5% resistance=220 package=THT]
  R22 = Resistor [tolerance=±5% resistance=220 package=THT]
  R23 = Resistor [tolerance=±5% resistance=220 package=THT]
  J1 = Piezo Speaker
  R24 = Resistor [tolerance=±5% resistance=220 package=THT]
  R25 = Resistor [tolerance=±5% resistance=10 package=THT]
  R26 = Resistor [tolerance=±5% resistance=10 package=THT]
  R27 = Resistor [tolerance=±5% resistance=10 package=THT]
  R28 = Resistor [tolerance=±5% resistance=10 package=THT]
  R29 = Resistor [tolerance=±5% resistance=10 package=THT]
  R30 = Resistor [tolerance=±5% resistance=10 package=THT]
  R31 = Resistor [tolerance=±5% resistance=10 package=THT]

nets:
  N1: Part1.A0, U4.DS
  N2: Part1.A1, U3.ST_CP, U4.ST_CP
  N3: Part1.A2, U3.SH_CP, U4.SH_CP
  N4: Part1.A3, U5.DS
  N5: Part1.A4/SDA, U5.ST_CP
  N6: Part1.A5/SCL, U5.SH_CP
  N7: Part1.D11_PWM/MOSI, R24.Pin_1
  N8: Part1.D12/MISO, R1.Pin_1
  N9: Part1.D13/SCK, DFRobot_DFPlayer_Mini1.TX
  GND: Part1.GND, Part1.D0/RX, Part1.D1/TX, Part1.D2, Part1.D3_PWM, Part1.D4, Part1.D5_PWM, Part1.D6_PWM, DFRobot_DFPlayer_Mini1.GND-1, DFRobot_DFPlayer_Mini1.GND-2, U3.GND, U3.OE, U4.GND, U4.OE, S2.Pin_1, S2.Pin_2, S2.Pin_3, S2.Pin_4, S5.Pin_1, S5.Pin_2, S5.Pin_3, S5.Pin_4, LED3.cathode, LED4.cathode, S6.Pin_1, S6.Pin_2, S6.Pin_3, S6.Pin_4, S7.Pin_1, S7.Pin_2, S7.Pin_3, S7.Pin_4, LED5.cathode, LED6.cathode, S8.Pin_1, S8.Pin_2, S8.Pin_3, S8.Pin_4, S9.Pin_1, S9.Pin_2, S9.Pin_3, S9.Pin_4, LED7.cathode, LED8.cathode, S10.Pin_1, S10.Pin_2, S10.Pin_3, S10.Pin_4, LED9.cathode, U5.GND, U5.OE, J1.pin1, R25.Pin_0, R26.Pin_0, R27.Pin_0, R28.Pin_0, R29.Pin_0, R30.Pin_0, R31.Pin_0
  VCC: Part1.5V, DFRobot_DFPlayer_Mini1.VCC, U3.MR, U3.VCC, U4.MR, U4.VCC, U5.VCC, R25.Pin_1, R26.Pin_1, R27.Pin_1, R28.Pin_1, R29.Pin_1, R30.Pin_1, R31.Pin_1
  N10: DFRobot_DFPlayer_Mini1.RX, R1.Pin_0
  N11: DFRobot_DFPlayer_Mini1.SPK_1, SP1.-
  N12: DFRobot_DFPlayer_Mini1.SPK_2, SP1.+
  N13: U1.E, R16.Pin_1
  N14: U1.D, R3.Pin_1
  N15: U1.G1, R4.Pin_1
  N16: U1.DP, R5.Pin_1
  N17: U1.A, R6.Pin_1
  N18: U1.G2, R7.Pin_1
  N19: U1.F, U2.F
  N20: U1.G, R2.Pin_1
  N21: U2.E, R8.Pin_1
  N22: U2.D, R13.Pin_1
  N23: U2.G1, R11.Pin_1
  N24: U2.DP, R14.Pin_1
  N25: U2.A, R15.Pin_1
  N26: U2.G2, R10.Pin_1
  N27: U2.G, R9.Pin_1
  N28: U3.Q1, R15.Pin_0
  N29: U3.Q2, R14.Pin_0
  N30: U3.Q3, R11.Pin_0
  N31: U3.Q4, R13.Pin_0
  N32: U3.Q5, R9.Pin_0
  N33: U3.Q6, R8.Pin_0
  N34: U3.DS, U4.Q7'
  N35: U3.Q0, R10.Pin_0
  N36: U4.Q1, R6.Pin_0
  N37: U4.Q2, R5.Pin_0
  N38: U4.Q3, R4.Pin_0
  N39: U4.Q4, R3.Pin_0
  N40: U4.Q5, R2.Pin_0
  N41: U4.Q6, R16.Pin_0
  N42: U4.Q0, R7.Pin_0
  N43: LED3.anode, R23.Pin_1
  N44: LED4.anode, R22.Pin_1
  N45: LED5.anode, R21.Pin_1
  N46: LED6.anode, R20.Pin_1
  N47: LED7.anode, R19.Pin_1
  N48: LED8.anode, R17.Pin_1
  N49: LED9.anode, R18.Pin_1
  N50: U5.Q1, R22.Pin_0
  N51: U5.Q2, R21.Pin_0
  N52: U5.Q3, R20.Pin_0
  N53: U5.Q4, R19.Pin_0
  N54: U5.Q5, R17.Pin_0
  N55: U5.Q6, R18.Pin_0
  N56: U5.Q0, R23.Pin_0
  N57: J1.pin2, R24.Pin_0
